// Logisim project design.circ as structural Verilog: 4 circuits, main circuit main
module main (
  output [6:0] out_1
);

  wire AC_out, analizadorteclado_1_out_4, clock_1_out;
  wire [6:0] analizadorteclado_1_salida_ascii, analizadorteclado_1_salida_binario;
  wire [18:0] _1_out;

  Clock clock_1 (.out(clock_1_out));
  AnalizadorTeclado analizadorteclado_1 (
    .Entrada(_1_out), .Salida_ASCII(analizadorteclado_1_salida_ascii),
    .Salida_binario(analizadorteclado_1_salida_binario), .out_4(analizadorteclado_1_out_4));
  MemoriaInstrucciones memoriainstrucciones_1 (
    .Entrada(analizadorteclado_1_salida_binario), .Reloj(clock_1_out), ._0_leer_1_escribir(_1_out[10]),
    .Salida(out_1));
  TTY #(.rows(1), .cols(30)) tty_1 (
    .data(analizadorteclado_1_salida_ascii), .clk(analizadorteclado_1_out_4), .clr(AC_out));  // open: we
  Button _1 (.out(_1_out[0]));
  Button _2 (.out(_1_out[1]));
  Button _4 (.out(_1_out[3]));
  Button _5 (.out(_1_out[4]));
  Button _8 (.out(_1_out[7]));
  Button _7 (.out(_1_out[6]));
  Button _0 (.out(_1_out[9]));
  Button AC (.out(AC_out));
  Button _3 (.out(_1_out[2]));
  Button _6 (.out(_1_out[5]));
  Button _9 (.out(_1_out[8]));
  Button button (.out(_1_out[10]));
  Button button_2 (.out(_1_out[14]));
  Button button_3 (.out(_1_out[18]));
  Button button_4 (.out(_1_out[13]));
  Button button_5 (.out(_1_out[17]));
  Button x (.out(_1_out[12]));
  Button button_6 (.out(_1_out[16]));
  Button button_7 (.out(_1_out[11]));
  Button x_y (.out(_1_out[15]));
endmodule

module AnalizadorTeclado (
  input  [18:0] Entrada,
  output [6:0] Salida_ASCII,
  output [6:0] Salida_binario,
  output out_4
);

  ROM #(.addrWidth(19), .dataWidth(7), .Select("low")) rom_1 (.addr(Entrada), .data(Salida_ASCII));
  ROM #(.addrWidth(19), .dataWidth(7), .Select("low")) rom_2 (.addr(Entrada), .data(Salida_binario));
  or or_1 (out_4, Salida_ASCII[0], Salida_ASCII[1], Salida_ASCII[2], Salida_ASCII[3], Salida_ASCII[4], Salida_ASCII[5], Salida_ASCII[6]);

  // Notes on the sheet:
  //   contents of rom_1 (hex, n*v repeats v):
  //   0 31 32 0 33 0 0 0 34 7*0 35 15*0 36 31*0 37 63*0 38 127*0 39 255*0 30 511*0 3d 1023*0 21 2047*0 2a
  //   4095*0 2b 8191*0 28 16383*0 5e 32767*0 25 65535*0 2d 131071*0 29
  //   contents of rom_2 (hex, n*v repeats v):
  //   0 1 2 0 3 0 0 0 4 7*0 5 15*0 6 31*0 7 63*0 8 127*0 9 767*0 3d 1023*0 21 2047*0 2a 4095*0 2b 8191*0
  //   28 16383*0 5e 32767*0 25 65535*0 2d 131071*0 29
endmodule

module Potenciador (
  input  [15:0] Base,
  input  [15:0] Exponente,
  input  Reloj,
  output [15:0] Salida
);

  wire comparator_1_eq, comparator_2_eq, not_1_out, register_3_q;
  wire [15:0] counter_1_q, multiplexer_1_out, multiplier_1_out, register_1_q, register_2_q;

  Multiplexer #(.width(16), .enable("false")) multiplexer_1 (
    .in0(Base), .in1(multiplier_1_out), .out(multiplexer_1_out), .sel(not_1_out));
  not not_1 (not_1_out, comparator_2_eq);
  Register #(.width(16), .Select("low")) register_1 (.D(Exponente), .Q(register_1_q), .clk(Reloj));  // open: en, clr
  Counter #(.width(16), .max('hffff)) counter_1 (
    .Q(counter_1_q), .clk(Reloj), .clr(register_3_q));  // open: load, D, count, carry, preset, down
  Register #(.width(16), .Select("low")) register_2 (
    .D(multiplexer_1_out), .Q(register_2_q), .clk(Reloj));  // open: en, clr
  Comparator #(.width(16)) comparator_1 (.a(register_1_q), .b(counter_1_q), .eq(comparator_1_eq));  // open: gt, lt
  Comparator #(.width(16)) comparator_2 (.a(counter_1_q), .b({16{1'b0}}), .eq(comparator_2_eq));  // open: gt, lt
  Multiplier #(.width(16)) multiplier_1 (.a(register_2_q), .b(Base), .out(multiplier_1_out));  // open: cin, cout
  Register #(.width(1), .Select("low")) register_3 (
    .D(comparator_1_eq), .Q(register_3_q), .clk(Reloj));  // open: en, clr
  Register #(.width(16), .Select("low")) register_4 (
    .D(register_2_q), .en(comparator_1_eq), .Q(Salida), .clk(Reloj));  // open: clr

  // Notes on the sheet:
  //   Contador
endmodule

module MemoriaInstrucciones (
  input  [6:0] Entrada,
  input  Reloj,
  input  _0_leer_1_escribir,
  output [6:0] Salida
);

  wire d_ff_1_q, d_ff_1_qn;
  wire [6:0] controlled_buffer_1_out, counter_1_q;

  Counter #(.width(7), .max('h7f)) counter_1 (
    .Q(counter_1_q), .clk(Reloj), .clr(_0_leer_1_escribir));  // open: load, D, count, carry, preset, down
  D_Flip_Flop d_ff_1 (.clk(Reloj), .D(_0_leer_1_escribir), .Q(d_ff_1_q), .Qn(d_ff_1_qn));  // open: preset, reset
  assign controlled_buffer_1_out = d_ff_1_qn ? Entrada : 7'bz;  // Controlled_Buffer controlled_buffer_1
  RAM #(.addrWidth(7), .dataWidth(7), .Select("low")) ram_1 (
    .addr(counter_1_q), .data(controlled_buffer_1_out), .clk(Reloj), .ld(d_ff_1_q));  // open: sel, clr
  assign Salida = d_ff_1_q ? controlled_buffer_1_out : 7'bz;  // Controlled_Buffer controlled_buffer_2
endmodule
